// Logisim project IT012_Lab01_25520730.circ as structural Verilog: 5 circuits, main circuit TN3
module TN3 (
  input  A,
  input  B,
  input  C,
  input  D,
  output F
);

  wire and_1_out, and_2_out, and_3_out, and_4_out, and_5_out, and_6_out, not_1_out, not_2_out, not_3_out,
       not_4_out;

  not not_1 (not_1_out, A);
  not not_2 (not_2_out, B);
  not not_3 (not_3_out, C);
  not not_4 (not_4_out, D);
  and and_1 (and_1_out, not_1_out, not_2_out, C, not_4_out);
  and and_2 (and_2_out, not_1_out, not_2_out, C, D);
  and and_3 (and_3_out, not_1_out, B, not_3_out, D);
  and and_4 (and_4_out, not_1_out, B, C, D);
  and and_5 (and_5_out, A, not_2_out, C, D);
  and and_6 (and_6_out, A, B, not_3_out, D);
  or or_1 (F, and_1_out, and_2_out, and_3_out, and_4_out, and_5_out, and_6_out);
endmodule

module TN1 (
  input  A,
  input  B,
  input  C,
  output A1,
  output cAND,
  output cOR,
  output cNAND,
  output cNOR,
  output cXOR,
  output cXNOR,
  output cXOR3,
  output cNAND3,
  output CHAIN
);

  wire X_out;

  not not_1 (A1, A);
  and and_1 (cAND, A, B);
  or or_1 (cOR, A, B);
  nand nand_1 (cNAND, A, B);
  nor nor_1 (cNOR, A, B);
  xor xor_1 (cXOR, A, B);
  xnor xnor_1 (cXNOR, A, B);
  xor xor_2 (cXOR3, A, B, C);
  nand nand_2 (cNAND3, A, B, C);
  nand X (X_out, B, A);
  nand Y (CHAIN, X_out, C);
endmodule

module TN2 (
  input  X,
  input  Y,
  input  Z,
  output BTieuThuc1,
  output BieuThuc2,
  output BieuThuc3,
  output BieuThuc4,
  output BieuThuc5
);

  wire and_1_out, and_2_out, and_3_out, and_4_out, and_5_out, and_6_out, not_1_out, not_2_out, not_3_out,
       not_4_out, not_5_out, not_6_out, not_7_out, or_1_out, or_2_out, or_3_out, or_4_out, or_5_out, or_6_out;

  not not_1 (not_1_out, X);
  not not_2 (not_2_out, Y);
  and and_1 (and_1_out, X, Y);
  not not_3 (not_3_out, X);
  not not_4 (not_4_out, Y);
  not not_5 (not_5_out, X);
  or or_1 (or_1_out, X, Y);
  and and_2 (and_2_out, not_1_out, not_2_out);
  and and_3 (and_3_out, Y, Z);
  and and_4 (and_4_out, Y, not_5_out);
  or or_2 (or_2_out, Y, X);
  not not_6 (not_6_out, or_1_out);
  not not_7 (not_7_out, and_1_out);
  and and_5 (and_5_out, not_3_out, not_4_out);
  or or_3 (or_3_out, Y, X);
  or or_4 (or_4_out, X, Z);
  or or_5 (or_5_out, and_3_out, X);
  or or_6 (or_6_out, and_4_out, X);
  xnor xnor_1 (BTieuThuc1, not_6_out, and_2_out);
  xnor xnor_2 (BieuThuc2, not_7_out, and_5_out);
  and and_6 (and_6_out, or_3_out, or_4_out);
  xnor xnor_3 (BieuThuc4, or_6_out, X);
  xnor xnor_4 (BieuThuc5, or_6_out, or_2_out);
  xnor xnor_5 (BieuThuc3, or_5_out, and_6_out);
endmodule

module TN4 (
  input  A,
  input  B,
  input  C,
  input  D,
  output EQ2,
  output EQ1
);

  wire and_1_out, and_2_out, and_3_out, and_4_out, and_5_out, and_6_out, and_7_out, and_8_out, and_9_out,
       and_10_out, Fcan_out, Fpos_out, Fsop_out, not_1_out, not_2_out, not_3_out, not_4_out, or_1_out,
       or_2_out, or_3_out, or_4_out;

  not not_1 (not_1_out, A);
  not not_2 (not_2_out, B);
  not not_3 (not_3_out, C);
  not not_4 (not_4_out, D);
  or or_1 (or_1_out, not_1_out, not_2_out, not_3_out);
  or or_2 (or_2_out, not_1_out, D);
  or or_3 (or_3_out, not_2_out, D);
  or or_4 (or_4_out, B, C);
  and and_1 (and_1_out, not_1_out, not_2_out, C, not_4_out);
  and and_2 (and_2_out, not_1_out, not_2_out, C, D);
  and and_3 (and_3_out, not_1_out, B, not_3_out, D);
  and and_4 (and_4_out, not_1_out, B, C, D);
  and and_5 (and_5_out, A, not_2_out, C, D);
  and and_6 (and_6_out, A, B, not_3_out, D);
  and and_7 (and_7_out, D, C, not_1_out);
  and and_8 (and_8_out, D, not_3_out, B);
  and and_9 (and_9_out, D, C, not_2_out);
  and and_10 (and_10_out, C, not_2_out, not_1_out);
  and Fpos (Fpos_out, or_1_out, or_2_out, or_3_out, or_4_out);
  or Fcan (Fcan_out, and_1_out, and_2_out, and_3_out, and_4_out, and_5_out, and_6_out);
  or Fsop (Fsop_out, and_7_out, and_8_out, and_9_out, and_10_out);
  xnor xnor_1 (EQ2, Fpos_out, Fcan_out);
  xnor xnor_2 (EQ1, Fcan_out, Fsop_out);
endmodule

module TN5 (
  input  A,
  input  B,
  input  C,
  output F
);

  wire xor_1_out;

  xor xor_1 (xor_1_out, A, B);
  xor xor_2 (F, xor_1_out, C);
endmodule
