// Logisim project TN2_25520730.circ as structural Verilog: 1 circuit, main circuit main
module main (
  input  X,
  input  Y,
  input  Z,
  output BTieuThuc1,
  output BieuThuc2,
  output BieuThuc3,
  output BieuThuc4,
  output BieuThuc5
);

  wire and_1_out, and_2_out, and_3_out, and_4_out, and_5_out, and_6_out, not_1_out, not_2_out, not_3_out,
       not_4_out, not_5_out, not_6_out, not_7_out, or_1_out, or_2_out, or_3_out, or_4_out, or_5_out, or_6_out;

  not not_1 (not_1_out, X);
  not not_2 (not_2_out, Y);
  and and_1 (and_1_out, X, Y);
  not not_3 (not_3_out, X);
  not not_4 (not_4_out, Y);
  not not_5 (not_5_out, X);
  or or_1 (or_1_out, X, Y);
  and and_2 (and_2_out, not_1_out, not_2_out);
  and and_3 (and_3_out, Y, Z);
  and and_4 (and_4_out, Y, not_5_out);
  or or_2 (or_2_out, Y, X);
  not not_6 (not_6_out, or_1_out);
  not not_7 (not_7_out, and_1_out);
  and and_5 (and_5_out, not_3_out, not_4_out);
  or or_3 (or_3_out, Y, X);
  or or_4 (or_4_out, X, Z);
  or or_5 (or_5_out, and_3_out, X);
  or or_6 (or_6_out, and_4_out, X);
  xnor xnor_1 (BTieuThuc1, not_6_out, and_2_out);
  xnor xnor_2 (BieuThuc2, not_7_out, and_5_out);
  and and_6 (and_6_out, or_3_out, or_4_out);
  xnor xnor_3 (BieuThuc4, or_6_out, X);
  xnor xnor_4 (BieuThuc5, or_6_out, or_2_out);
  xnor xnor_5 (BieuThuc3, or_5_out, and_6_out);
endmodule
